# Fritzing sketch board (saved by Fritzing 0.9.3b)
breadboards: 2

parts:
  Part1 = Arduino Uno (Rev3)
  Part3 = Arduino Nano (Rev3.0)
  Part4 = RFID-RC522-v2
  R2 = Resistor [tolerance=±5% resistance=1k package="0603 [SMD]"]
  DHT1 = DHT11 Humitidy and Temperature Sensor
  SERVO1 = Tower Pro SG90 servo [part_number=101246]

nets:
  N1: Part1.A4/SDA, Part3.A4
  N2: Part1.A5/SCL, Part3.A5
  N3: Part1.D10_PWM/SS, SERVO1.Signal
  5V: Part1.5V, Part3.VIN, R2.Pin_0, DHT1.VDD, SERVO1.+5V
  GND: Part1.GND, Part3.GND, Part4.GND, DHT1.GND, SERVO1.GND
  N4: Part3.D9, Part4.RST
  N5: Part3.D10, Part4.SDA
  N6: Part3.D11/MOSI, Part4.MOSI
  N7: Part3.D12/MISO, Part4.MISO
  N8: Part3.A2, R2.Pin_1, DHT1.DATA
  3V3: Part3.3V3, Part4.3.3V
  N9: Part3.D13/SCK, Part4.SCK

custom parts:
  RFID-RC522-v2: A simple China made RFID-RC522 Reader; do check the pin labels, as this is a MFRC522 based clone.
  DHT11 Humitidy and Temperature Sensor: DHT11 Humidity and Temperature Sensor
  Tower Pro SG90 servo: Original file by John De Cristofaro http://www.adafruit.com/products/1449 Adafruit Feedback Servo (Small) Edited by: e-radionica.com 28/9/2015
